// Logisim project aula_2.circ as structural Verilog: 5 circuits, main circuit main
module main (
  input  [3:0] in_1,
  input  [3:0] in_2,
  input  in_3,
  input  in_4,
  input  in_5,
  input  in_6,
  input  in_7,
  input  in_8,
  input  [3:0] in_9,
  input  [3:0] in_10,
  input  in_11,
  input  in_12,
  output out_13,
  output out_14,
  output out_15,
  output [3:0] out_16,
  output out_17,
  output out_18,
  output out_19,
  output [3:0] out_20
);

  ADD_1 add_1_1 (.A(in_3), .B(in_4), .Vem_1(in_5), .S(out_15), .Vai_1(out_13));
  SUB_1 sub_1_1 (.A(in_7), .B(in_8), .Vem_1(in_11), .S(out_19), .Vai_1(out_17));
  ADD_4 add_4_1 (.A(in_1), .out_4(out_14), .B(in_2), .in_3(in_6), .out_5(out_16));
  SUB_4 sub_4_1 (.A(in_9), .out_4(out_18), .B(in_10), .in_3(in_12), .out_5(out_20));
endmodule

module ADD_1 (
  input  A,
  input  B,
  input  Vem_1,
  output S,
  output Vai_1
);

  wire and_1_out, and_2_out, or_1_out, xor_1_out;

  xor xor_1 (xor_1_out, A, B);
  or or_1 (or_1_out, B, Vem_1);
  and and_1 (and_1_out, B, Vem_1);
  and and_2 (and_2_out, or_1_out, A);
  xor xor_2 (S, xor_1_out, Vem_1);
  or or_2 (Vai_1, and_2_out, and_1_out);
endmodule

module ADD_4 (
  input  [3:0] A,
  input  [3:0] B,
  input  in_3,
  output out_4,
  output [3:0] out_5
);

  wire add_1_2_vai_1, add_1_3_vai_1, add_1_4_vai_1;

  ADD_1 add_1_1 (.A(A[3]), .B(B[3]), .Vem_1(add_1_2_vai_1), .S(out_5[3]), .Vai_1(out_4));
  ADD_1 add_1_2 (.A(A[2]), .B(B[2]), .Vem_1(add_1_3_vai_1), .S(out_5[2]), .Vai_1(add_1_2_vai_1));
  ADD_1 add_1_3 (.A(A[1]), .B(B[1]), .Vem_1(add_1_4_vai_1), .S(out_5[1]), .Vai_1(add_1_3_vai_1));
  ADD_1 add_1_4 (.A(A[0]), .B(B[0]), .Vem_1(in_3), .S(out_5[0]), .Vai_1(add_1_4_vai_1));
endmodule

module SUB_1 (
  input  A,
  input  B,
  input  Vem_1,
  output S,
  output Vai_1
);

  wire and_1_out, and_2_out, not_1_out, or_1_out, xor_1_out;

  xor xor_1 (xor_1_out, A, B);
  or or_1 (or_1_out, B, Vem_1);
  not not_1 (not_1_out, A);
  and and_1 (and_1_out, B, Vem_1);
  and and_2 (and_2_out, or_1_out, not_1_out);
  xor xor_2 (S, xor_1_out, Vem_1);
  or or_2 (Vai_1, and_2_out, and_1_out);
endmodule

module SUB_4 (
  input  [3:0] A,
  input  [3:0] B,
  input  in_3,
  output out_4,
  output [3:0] out_5
);

  wire sub_1_2_vai_1, sub_1_3_vai_1, sub_1_4_vai_1;

  SUB_1 sub_1_1 (.A(A[3]), .B(B[3]), .Vem_1(sub_1_2_vai_1), .S(out_5[3]), .Vai_1(out_4));
  SUB_1 sub_1_2 (.A(A[2]), .B(B[2]), .Vem_1(sub_1_3_vai_1), .S(out_5[2]), .Vai_1(sub_1_2_vai_1));
  SUB_1 sub_1_3 (.A(A[1]), .B(B[1]), .Vem_1(sub_1_4_vai_1), .S(out_5[1]), .Vai_1(sub_1_3_vai_1));
  SUB_1 sub_1_4 (.A(A[0]), .B(B[0]), .Vem_1(in_3), .S(out_5[0]), .Vai_1(sub_1_4_vai_1));
endmodule
