// Logisim project cpu_risc_atualizado.circ as structural Verilog: 16 circuits, main circuit main
module main (
  input  R___1___W___0,
  output Ovf,
  output Zero
);

  wire alu_1_overflow, alu_1_zero, clock_1_out, not_1_out, Reset_out, unidade_de_controle_1_clk_ac,
       unidade_de_controle_1_clk_pc, unidade_de_controle_1_clk_ram, unidade_de_controle_1_clk_rl,
       \unidade_de_controle_1_direção , unidade_de_controle_1_e, unidade_de_controle_1_rst_pc;
  wire [2:0] \unidade_de_controle_1_operação ;
  wire [3:0] ac_1_q, alu_1_out_6, counter_1_q, mux_1_s, ram_1_data, \unidade_de_controle_1_b_endereços ,
       unidade_de_controle_1_operando;
  wire [7:0] ir_1_q, rom_1_data;

  Counter #(.width(4), .max('hf)) counter_1 (
    .Q(counter_1_q), .clk(unidade_de_controle_1_clk_rl), .clr(unidade_de_controle_1_rst_pc));  // open: load, D, count, carry
  Clock clock_1 (.out(clock_1_out));
  Button Reset (.out(Reset_out));
  ROM #(.addrWidth(4)) rom_1 (.addr(counter_1_q), .data(rom_1_data));  // open: sel
  IR ir_1 (.Clock(unidade_de_controle_1_clk_pc), .Q(ir_1_q), .D(rom_1_data));
  Unidade_de_controle unidade_de_controle_1 (
    .\B_endereços (\unidade_de_controle_1_b_endereços ), .Operando(unidade_de_controle_1_operando),
    .\Direção (\unidade_de_controle_1_direção ), .E(unidade_de_controle_1_e),
    .\Operação (\unidade_de_controle_1_operação ), .\Instrução (ir_1_q), .Clock(clock_1_out),
    .Reset(Reset_out), .Rst_PC(unidade_de_controle_1_rst_pc), .clk_Rl(unidade_de_controle_1_clk_rl),
    .clk_AC(unidade_de_controle_1_clk_ac), .clk_PC(unidade_de_controle_1_clk_pc),
    .clk_RAM(unidade_de_controle_1_clk_ram));
  // Probe on ac_1_q
  AC ac_1 (.Q(ac_1_q), .D(alu_1_out_6), .Clock(unidade_de_controle_1_clk_ac));
  MUX mux_1 (.E(unidade_de_controle_1_operando), .Controle(unidade_de_controle_1_e), .D(ram_1_data), .S(mux_1_s));
  // Probe on mux_1_s
  ALU alu_1 (
    .D(\unidade_de_controle_1_direção ), .A(ac_1_q), .B(mux_1_s),
    .\Operações (\unidade_de_controle_1_operação ), .out_6(alu_1_out_6), .Overflow(alu_1_overflow),
    .Zero(alu_1_zero));
  // Probe on alu_1_out_6
  D_Flip_Flop d_ff_1 (.clk(unidade_de_controle_1_clk_ac), .D(alu_1_overflow), .Q(Ovf));  // open: Qn, preset, en, reset
  D_Flip_Flop d_ff_2 (.clk(unidade_de_controle_1_clk_ac), .D(alu_1_zero), .Q(Zero));  // open: Qn, preset, en, reset
  RAM #(.addrWidth(4), .dataWidth(4)) ram_1 (
    .addr(\unidade_de_controle_1_b_endereços ), .data(ram_1_data), .clk(unidade_de_controle_1_clk_ram),
    .ld(R___1___W___0));  // open: sel, clr
  not not_1 (not_1_out, R___1___W___0);
  BUFFER buffer_1 (.in_2(not_1_out), .in_1(ac_1_q), .out_3(ram_1_data));

  // Notes on the sheet:
  //   contents of rom_1 (hex, n*v repeats v):
  //   0 f0 1 f1 10 31 d0 f2 11 f0 12 f1 e4
endmodule

module ADD_1 (
  input  A,
  input  B,
  input  Vem_1,
  output S,
  output Vai_1
);

  wire and_1_out, and_2_out, or_1_out, xor_1_out;

  xor xor_1 (xor_1_out, A, B);
  or or_1 (or_1_out, B, Vem_1);
  and and_1 (and_1_out, B, Vem_1);
  and and_2 (and_2_out, or_1_out, A);
  xor xor_2 (S, xor_1_out, Vem_1);
  or or_2 (Vai_1, and_2_out, and_1_out);
endmodule

module ADD_4 (
  input  [3:0] A,
  input  [3:0] B,
  input  in_3,
  output out_4,
  output [3:0] out_5
);

  wire add_1_2_vai_1, add_1_3_vai_1, add_1_4_vai_1;

  ADD_1 add_1_1 (.A(A[3]), .B(B[3]), .Vem_1(add_1_2_vai_1), .S(out_5[3]), .Vai_1(out_4));
  ADD_1 add_1_2 (.A(A[2]), .B(B[2]), .Vem_1(add_1_3_vai_1), .S(out_5[2]), .Vai_1(add_1_2_vai_1));
  ADD_1 add_1_3 (.A(A[1]), .B(B[1]), .Vem_1(add_1_4_vai_1), .S(out_5[1]), .Vai_1(add_1_3_vai_1));
  ADD_1 add_1_4 (.A(A[0]), .B(B[0]), .Vem_1(in_3), .S(out_5[0]), .Vai_1(add_1_4_vai_1));
endmodule

module SUB_1 (
  input  A,
  input  B,
  input  Vem_1,
  output S,
  output Vai_1
);

  wire and_1_out, and_2_out, not_1_out, or_1_out, xor_1_out;

  xor xor_1 (xor_1_out, A, B);
  or or_1 (or_1_out, B, Vem_1);
  not not_1 (not_1_out, A);
  and and_1 (and_1_out, B, Vem_1);
  and and_2 (and_2_out, or_1_out, not_1_out);
  xor xor_2 (S, xor_1_out, Vem_1);
  or or_2 (Vai_1, and_2_out, and_1_out);
endmodule

module SUB_4 (
  input  [3:0] A,
  input  [3:0] B,
  input  in_3,
  output out_4,
  output [3:0] out_5
);

  wire sub_1_2_vai_1, sub_1_3_vai_1, sub_1_4_vai_1;

  SUB_1 sub_1_1 (.A(A[3]), .B(B[3]), .Vem_1(sub_1_2_vai_1), .S(out_5[3]), .Vai_1(out_4));
  SUB_1 sub_1_2 (.A(A[2]), .B(B[2]), .Vem_1(sub_1_3_vai_1), .S(out_5[2]), .Vai_1(sub_1_2_vai_1));
  SUB_1 sub_1_3 (.A(A[1]), .B(B[1]), .Vem_1(sub_1_4_vai_1), .S(out_5[1]), .Vai_1(sub_1_3_vai_1));
  SUB_1 sub_1_4 (.A(A[0]), .B(B[0]), .Vem_1(in_3), .S(out_5[0]), .Vai_1(sub_1_4_vai_1));
endmodule

module BUFFER (
  input  [3:0] in_1,
  input  in_2,
  output [3:0] out_3
);

  assign out_3[3] = in_2 ? in_1[3] : 1'bz;  // Controlled_Buffer controlled_buffer_1
  assign out_3[2] = in_2 ? in_1[2] : 1'bz;  // Controlled_Buffer controlled_buffer_2
  assign out_3[1] = in_2 ? in_1[1] : 1'bz;  // Controlled_Buffer controlled_buffer_3
  assign out_3[0] = in_2 ? in_1[0] : 1'bz;  // Controlled_Buffer controlled_buffer_4
endmodule

module DECODER (
  input  [2:0] in_1,
  output out_2,
  output out_3,
  output out_4,
  output out_5,
  output out_6,
  output out_7,
  output out_8,
  output out_9
);

  and and_1 (out_2, ~in_1[2], ~in_1[1], ~in_1[0]);  // AND_Gate
  and and_2 (out_3, ~in_1[2], ~in_1[1], in_1[0]);  // AND_Gate
  and and_3 (out_4, ~in_1[2], in_1[1], ~in_1[0]);  // AND_Gate
  and and_4 (out_5, ~in_1[2], in_1[1], in_1[0]);  // AND_Gate
  and and_5 (out_6, in_1[2], ~in_1[1], ~in_1[0]);  // AND_Gate
  and and_6 (out_7, in_1[2], ~in_1[1], in_1[0]);  // AND_Gate
  and and_7 (out_8, in_1[2], in_1[1], ~in_1[0]);  // AND_Gate
  and and_8 (out_9, in_1[2], in_1[1], in_1[0]);
endmodule

module BUFFER_N (
  input  [3:0] in_1,
  input  in_2,
  output [3:0] out_3
);

  assign out_3[3] = in_2 ? ~in_1[3] : 1'bz;  // Controlled_Inverter controlled_inverter_1
  assign out_3[2] = in_2 ? ~in_1[2] : 1'bz;  // Controlled_Inverter controlled_inverter_2
  assign out_3[1] = in_2 ? ~in_1[1] : 1'bz;  // Controlled_Inverter controlled_inverter_3
  assign out_3[0] = in_2 ? ~in_1[0] : 1'bz;  // Controlled_Inverter controlled_inverter_4
endmodule

module Rot_L (
  input  [3:0] A_B_C_D,
  input  [1:0] X_Y,
  output [3:0] out_3
);

  wire and_1_out, and_2_out, and_3_out, and_4_out, and_5_out, and_6_out, and_7_out, and_8_out, and_9_out;

  and and_1 (and_1_out, ~X_Y[1], ~X_Y[0], A_B_C_D[3]);  // AND_Gate
  and and_2 (and_2_out, ~X_Y[1], X_Y[0], A_B_C_D[2]);  // AND_Gate
  and and_3 (and_3_out, X_Y[1], ~X_Y[0], A_B_C_D[1]);  // AND_Gate
  and and_4 (and_4_out, X_Y[1], X_Y[0], A_B_C_D[0]);
  and and_5 (and_5_out, ~X_Y[1], ~X_Y[0], A_B_C_D[2]);  // AND_Gate
  and and_6 (and_6_out, ~X_Y[1], X_Y[0], A_B_C_D[1]);  // AND_Gate
  and and_7 (and_7_out, X_Y[1], ~X_Y[0], A_B_C_D[0]);  // AND_Gate
  and and_8 (and_8_out, ~X_Y[1], ~X_Y[0], A_B_C_D[1]);  // AND_Gate
  and and_9 (and_9_out, ~X_Y[1], X_Y[0], A_B_C_D[0]);  // AND_Gate
  and and_10 (out_3[0], ~X_Y[1], ~X_Y[0], A_B_C_D[0]);  // AND_Gate
  or or_1 (out_3[3], and_1_out, and_2_out, and_3_out, and_4_out);
  or or_2 (out_3[2], and_5_out, and_6_out, and_7_out);
  or or_3 (out_3[1], and_8_out, and_9_out);
endmodule

module Rot_R (
  input  [3:0] A_B_C_D,
  input  [1:0] X_Y,
  output [3:0] out_3
);

  wire and_1_out, and_2_out, and_3_out, and_4_out, and_5_out, and_6_out, and_7_out, and_8_out, and_9_out;

  and and_1 (and_1_out, ~X_Y[1], ~X_Y[0], A_B_C_D[0]);  // AND_Gate
  and and_2 (and_2_out, ~X_Y[1], X_Y[0], A_B_C_D[1]);  // AND_Gate
  and and_3 (and_3_out, X_Y[1], ~X_Y[0], A_B_C_D[2]);  // AND_Gate
  and and_4 (and_4_out, X_Y[1], X_Y[0], A_B_C_D[3]);
  and and_5 (and_5_out, ~X_Y[1], ~X_Y[0], A_B_C_D[1]);  // AND_Gate
  and and_6 (and_6_out, ~X_Y[1], X_Y[0], A_B_C_D[2]);  // AND_Gate
  and and_7 (and_7_out, X_Y[1], ~X_Y[0], A_B_C_D[3]);  // AND_Gate
  and and_8 (and_8_out, ~X_Y[1], ~X_Y[0], A_B_C_D[2]);  // AND_Gate
  and and_9 (and_9_out, ~X_Y[1], X_Y[0], A_B_C_D[3]);  // AND_Gate
  and and_10 (out_3[3], ~X_Y[1], ~X_Y[0], A_B_C_D[3]);  // AND_Gate
  or or_1 (out_3[0], and_1_out, and_2_out, and_3_out, and_4_out);
  or or_2 (out_3[1], and_5_out, and_6_out, and_7_out);
  or or_3 (out_3[2], and_8_out, and_9_out);
endmodule

module OR_4 (
  input  [3:0] in_1,
  input  [3:0] in_2,
  output [3:0] out_3
);

  or or_1 (out_3[3], in_1[3], in_2[3]);
  or or_2 (out_3[2], in_1[2], in_2[2]);
  or or_3 (out_3[1], in_1[1], in_2[1]);
  or or_4 (out_3[0], in_1[0], in_2[0]);
endmodule

module ALU (
  input  D,
  input  [3:0] A,
  input  [3:0] B,
  input  [2:0] \Operações ,
  output Overflow,
  output [3:0] out_6,
  output Zero
);

  wire add_4_1_out_4, and_1_out, and_2_out, decoder_1_out_2, decoder_1_out_3, decoder_1_out_4,
       decoder_1_out_5, decoder_1_out_6, decoder_1_out_7, decoder_1_out_8, decoder_1_out_9, not_1_out,
       sub_4_1_out_4;
  wire [3:0] add_4_1_out_5, buffer_5_out_3, or_4_1_out_3, rot_l_1_out_3, rot_r_1_out_3, sub_4_1_out_5;

  or or_1 (Overflow, and_1_out, and_2_out);
  and and_1 (and_1_out, add_4_1_out_4, decoder_1_out_3);
  and and_2 (and_2_out, sub_4_1_out_4, decoder_1_out_4);
  DECODER decoder_1 (
    .in_1(\Operações ), .out_2(decoder_1_out_2), .out_3(decoder_1_out_3), .out_4(decoder_1_out_4),
    .out_5(decoder_1_out_5), .out_6(decoder_1_out_6), .out_7(decoder_1_out_7), .out_8(decoder_1_out_8),
    .out_9(decoder_1_out_9));
  nor nor_1 (Zero, decoder_1_out_9, decoder_1_out_8, out_6[0], out_6[1], out_6[2], out_6[3]);
  BUFFER buffer_1 (.in_2(decoder_1_out_2), .in_1(B), .out_3(out_6));
  ADD_4 add_4_1 (.A(A), .out_4(add_4_1_out_4), .B(B), .in_3(1'b0), .out_5(add_4_1_out_5));
  BUFFER buffer_2 (.in_2(decoder_1_out_3), .in_1(add_4_1_out_5), .out_3(out_6));
  SUB_4 sub_4_1 (.A(A), .out_4(sub_4_1_out_4), .B(B), .in_3(1'b0), .out_5(sub_4_1_out_5));
  BUFFER buffer_3 (.in_2(decoder_1_out_4), .in_1(sub_4_1_out_5), .out_3(out_6));
  OR_4 or_4_1 (.in_1(A), .in_2(B), .out_3(or_4_1_out_3));
  BUFFER buffer_4 (.in_2(decoder_1_out_5), .in_1(or_4_1_out_3), .out_3(out_6));
  BUFFER_N buffer_n_1 (.in_2(decoder_1_out_6), .in_1(B), .out_3(out_6));
  Rot_L rot_l_1 (.out_3(rot_l_1_out_3), .A_B_C_D(A), .X_Y(B[1:0]));
  not not_1 (not_1_out, D);
  Rot_R rot_r_1 (.out_3(rot_r_1_out_3), .A_B_C_D(A), .X_Y(B[1:0]));
  BUFFER buffer_5 (.in_2(not_1_out), .in_1(rot_l_1_out_3), .out_3(buffer_5_out_3));
  BUFFER buffer_6 (.in_2(decoder_1_out_7), .in_1(buffer_5_out_3), .out_3(out_6));
  BUFFER buffer_7 (.in_2(D), .in_1(rot_r_1_out_3), .out_3(buffer_5_out_3));
endmodule

module AC (
  input  Clock,
  input  [3:0] D,
  output [3:0] Q
);

  D_Flip_Flop d_ff_1 (.clk(Clock), .D(D[3]), .Q(Q[3]));  // open: Qn, preset, en, reset
  D_Flip_Flop d_ff_2 (.clk(Clock), .D(D[2]), .Q(Q[2]));  // open: Qn, preset, en, reset
  D_Flip_Flop d_ff_3 (.clk(Clock), .D(D[1]), .Q(Q[1]));  // open: Qn, preset, en, reset
  D_Flip_Flop d_ff_4 (.clk(Clock), .D(D[0]), .Q(Q[0]));  // open: Qn, preset, en, reset
endmodule

module MUX (
  input  [3:0] E,
  input  [3:0] D,
  input  Controle,
  output [3:0] S
);

  wire not_1_out;

  BUFFER buffer_1 (.in_2(not_1_out), .in_1(E), .out_3(S));
  not not_1 (not_1_out, Controle);
  BUFFER buffer_2 (.in_2(Controle), .in_1(D), .out_3(S));
endmodule

module IR (
  input  Clock,
  input  [7:0] D,
  output [7:0] Q
);

  D_Flip_Flop D3 (.clk(Clock), .D(D[7]), .Q(Q[7]));  // open: Qn, preset, en, reset
  D_Flip_Flop D2 (.clk(Clock), .D(D[6]), .Q(Q[6]));  // open: Qn, preset, en, reset
  D_Flip_Flop D1 (.clk(Clock), .D(D[5]), .Q(Q[5]));  // open: Qn, preset, en, reset
  D_Flip_Flop D3_2 (.clk(Clock), .D(D[3]), .Q(Q[3]));  // open: Qn, preset, en, reset
  D_Flip_Flop D0 (.clk(Clock), .D(D[4]), .Q(Q[4]));  // open: Qn, preset, en, reset
  D_Flip_Flop D2_2 (.clk(Clock), .D(D[2]), .Q(Q[2]));  // open: Qn, preset, en, reset
  D_Flip_Flop D1_2 (.clk(Clock), .D(D[1]), .Q(Q[1]));  // open: Qn, preset, en, reset
  D_Flip_Flop D0_2 (.clk(Clock), .D(D[0]), .Q(Q[0]));  // open: Qn, preset, en, reset
endmodule

module Unidade_de_controle (
  input  [7:0] \Instrução ,
  input  Clock,
  input  Reset,
  output [3:0] \B_endereços ,
  output clk_Rl,
  output clk_PC,
  output clk_AC,
  output clk_RAM,
  output [3:0] Operando,
  output Rst_PC,
  output \Direção ,
  output E,
  output [2:0] \Operação 
);

  wire nand_1_out;
  wire [1:0] counter_1_q;

  Counter #(.width(2), .max('h3)) counter_1 (.Q(counter_1_q), .clk(Clock), .clr(Reset));  // open: load, D, count, carry
  and and_1 (clk_Rl, ~counter_1_q[0], ~counter_1_q[1]);  // AND_Gate
  and and_2 (clk_PC, counter_1_q[0], ~counter_1_q[1]);  // AND_Gate
  and and_3 (clk_AC, ~counter_1_q[0], counter_1_q[1]);  // AND_Gate
  and and_4 (clk_RAM, counter_1_q[0], counter_1_q[1]);
  nand nand_1 (nand_1_out, \Instrução [7], ~\Instrução [6], \Instrução [5]);  // NAND_Gate
  and and_5 (E, \Instrução [4], nand_1_out);

  assign \B_endereços  = \Instrução [3:0];
  assign \Direção  = \Instrução [4];
  assign Operando = \Instrução [3:0];
  assign \Operação  = \Instrução [7:5];
  assign Rst_PC = Reset;
endmodule
